// Logisim project ALU.circ as structural Verilog
module HalfAdder (
  input  a,
  input  b,
  output sum,
  output carry
);

  xor XOR (sum, a, b);
  and OX (carry, a, b);

  // Notes on the sheet:
  //   Half Adder
endmodule

module FullAdder (
  input  a,
  input  b,
  input  c,
  output sum,
  output carry
);

  wire HalfAdder_2_carry, HalfAdder_carry, HalfAdder_sum;

  HalfAdder HalfAdder (.a(a), .b(b), .sum(HalfAdder_sum), .carry(HalfAdder_carry));
  HalfAdder HalfAdder_2 (.a(HalfAdder_sum), .b(c), .sum(sum), .carry(HalfAdder_2_carry));
  or or_1 (carry, HalfAdder_carry, HalfAdder_2_carry);

  // Notes on the sheet:
  //   FullAdder
endmodule

module Add16 (
  input  [15:0] in_1,
  input  [15:0] in_2,
  output [15:0] out_3
);

  wire FullAdder_carry, HalfAdder_carry;

  HalfAdder HalfAdder (.a(in_1[0]), .b(in_2[0]), .sum(out_3[0]), .carry(HalfAdder_carry));
  FullAdder FullAdder (.a(in_1[1]), .b(in_2[1]), .c(HalfAdder_carry), .sum(out_3[1]), .carry(FullAdder_carry));
  // FullAdder FullAdder_2: pin names not known; wires that end beside it: in_1[2], FullAdder_carry
endmodule
